// Logisim project threeAddress.circ as structural Verilog: 13 circuits, main circuit CPU-Main
module ALU (
  input  [15:0] AC,
  input  [15:0] Y,
  input  [3:0] ALUOp,
  output [15:0] Output,
  output Overflow
);

  wire adder_1_cout, adder_2_cout, xor_16_out;
  wire [14:0] xor_1_out;

  xor xor_1 (xor_1_out[0], Y[0], ALUOp[0]);
  xor xor_2 (xor_1_out[2], Y[2], ALUOp[0]);
  xor xor_3 (xor_1_out[4], Y[4], ALUOp[0]);
  xor xor_4 (xor_1_out[6], Y[6], ALUOp[0]);
  xor xor_5 (xor_1_out[8], Y[8], ALUOp[0]);
  xor xor_6 (xor_1_out[10], Y[10], ALUOp[0]);
  xor xor_7 (xor_1_out[12], Y[12], ALUOp[0]);
  xor xor_8 (xor_1_out[14], Y[14], ALUOp[0]);
  xor xor_9 (xor_1_out[1], Y[1], ALUOp[0]);
  xor xor_10 (xor_1_out[3], Y[3], ALUOp[0]);
  xor xor_11 (xor_1_out[5], Y[5], ALUOp[0]);
  xor xor_12 (xor_1_out[7], Y[7], ALUOp[0]);
  xor xor_13 (xor_1_out[9], Y[9], ALUOp[0]);
  xor xor_14 (xor_1_out[11], Y[11], ALUOp[0]);
  xor xor_15 (xor_1_out[13], Y[13], ALUOp[0]);
  xor xor_16 (xor_16_out, Y[15], ALUOp[0]);
  Adder #(.width(15)) adder_1 (.a(AC[14:0]), .b(xor_1_out), .out(Output[14:0]), .cin(ALUOp[0]), .cout(adder_1_cout));
  Adder #(.width(1)) adder_2 (.a(AC[15]), .b(xor_16_out), .out(Output[15]), .cin(adder_1_cout), .cout(adder_2_cout));
  xor xor_17 (Overflow, adder_1_cout, adder_2_cout);

  // Notes on the sheet:
  //   0000 = add
  //   0001 = sub
endmodule

module Control_Unit (
  input  [7:0] Instruction,
  output [3:0] ALUOp,
  output WriteAc,
  output ALUSrc,
  output ClrAC,
  output MemWr,
  output Branch,
  output BR
);

  ROM #(.addrWidth(4), .dataWidth(6)) rom_1 (
    .addr(Instruction[7:4]), .data({BR, Branch, MemWr, ClrAC, ALUSrc, WriteAc}));  // open: sel

  assign ALUOp = Instruction[3:0];

  // Notes on the sheet:
  //   contents of rom_1 (hex, n*v repeats v):
  //   0 3 1 5 8 10 20
  //   00 03 01 05
  //   08 10 20 00
endmodule

module SignExtend (
  input  [7:0] Immediate,
  output [15:0] SignExtValue
);


  assign SignExtValue = {{9{Immediate[7]}}, Immediate[6:0]};
endmodule

module CPU_Main (
);

  wire and_1_out, button_1_out, clock_1_out, comparator_1_eq, control_unit_1_alusrc, control_unit_1_br,
       control_unit_1_branch, control_unit_1_clrac, control_unit_1_memwr, control_unit_1_writeac, or_1_out;
  wire [3:0] control_unit_1_aluop;
  wire [7:0] adder_1_out, multiplexer_1_out, PC_q, ram_1_data;
  wire [15:0] AC_q, alu1_1_output, multiplexer_2_out, multiplexer_3_out, ram_2_data,
       signextend_1_signextvalue;
  wire [15:8] ram_1_data_2;

  Clock clock_1 (.out(clock_1_out));
  Button button_1 (.out(button_1_out));
  Adder adder_1 (.a(PC_q), .b(8'h1), .out(adder_1_out));  // open: cin, cout
  or or_1 (or_1_out, and_1_out, control_unit_1_br);
  and and_1 (and_1_out, comparator_1_eq, control_unit_1_branch);
  Multiplexer #(.width(8), .enable("false")) multiplexer_1 (
    .in0(adder_1_out), .in1(ram_1_data), .out(multiplexer_1_out), .sel(or_1_out));
  Register PC (.D(multiplexer_1_out), .en(1'b1), .Q(PC_q), .clk(clock_1_out), .clr(button_1_out));
  RAM #(.dataWidth(16)) ram_1 (
    .addr(PC_q), .data({ram_1_data_2, ram_1_data}), .clk(clock_1_out));  // open: sel, ld, clr
  Control_Unit control_unit_1 (
    .Instruction(ram_1_data_2), .ALUOp(control_unit_1_aluop), .WriteAc(control_unit_1_writeac),
    .ALUSrc(control_unit_1_alusrc), .ClrAC(control_unit_1_clrac), .MemWr(control_unit_1_memwr),
    .Branch(control_unit_1_branch), .BR(control_unit_1_br));
  RAM #(.dataWidth(16), .bus("separate")) ram_2 (
    .addr(ram_1_data), .din(AC_q), .data(ram_2_data), .str(control_unit_1_memwr), .sel(1'b1),
    .clk(clock_1_out), .ld(1'b1));  // open: clr
  SignExtend signextend_1 (.Immediate(ram_1_data), .SignExtValue(signextend_1_signextvalue));
  Multiplexer #(.width(16), .enable("false")) multiplexer_2 (
    .in0(alu1_1_output), .in1({16{1'b0}}), .out(multiplexer_2_out), .sel(control_unit_1_clrac));
  Register #(.width(16)) AC (
    .D(multiplexer_2_out), .en(control_unit_1_writeac), .Q(AC_q), .clk(clock_1_out), .clr(button_1_out));
  Multiplexer #(.width(16), .enable("false")) multiplexer_3 (
    .in0(ram_2_data), .in1(signextend_1_signextvalue), .out(multiplexer_3_out), .sel(control_unit_1_alusrc));
  Comparator #(.width(16)) comparator_1 (.a(AC_q), .b({16{1'b0}}), .eq(comparator_1_eq));  // open: gt, lt
  ALU1 alu1_1 (.AC(AC_q), .Y(multiplexer_3_out), .ALUOp(control_unit_1_aluop), .Output(alu1_1_output));

  // Notes on the sheet:
  //   Reset PC
  //   Increment PC
  //   Branch Address
  //   Next Instr
  //   Select Branch if Branc = true and ALU is zero
  //   Text (Program) Memory
  //   Control Unit
  //   Data Memory
  //   Sign Extend
  //   Mem Data
  //   Immediate
  //   AC tp Memory
  //   Select ALU Input
  //   AC to ALU
  //   ALU to AC
  //   ALU
  //   ALUOpt
endmodule

module CPU_Arithmetic_Subsection (
);

  wire undriven, undriven_2, undriven_3, undriven_4, undriven_5;
  wire [3:0] undriven_6;
  wire [15:0] AC_q, alu_1_output, multiplexer_1_out, multiplexer_2_out, ram_1_data, signextend_1_signextvalue;

  RAM #(.dataWidth(16), .bus("separate")) ram_1 (
    .addr({8{1'b0}}), .din(AC_q), .data(ram_1_data), .str(undriven), .sel(1'b1), .clk(undriven_2), .ld(1'b1));  // open: clr
  SignExtend signextend_1 (.Immediate({8{1'b0}}), .SignExtValue(signextend_1_signextvalue));
  Multiplexer #(.width(16), .enable("false")) multiplexer_1 (
    .in0(alu_1_output), .in1({16{1'b0}}), .out(multiplexer_1_out), .sel(undriven_3));
  Register #(.width(16)) AC (.D(multiplexer_1_out), .en(undriven_4), .Q(AC_q), .clk(undriven_2));  // open: clr
  Multiplexer #(.width(16), .enable("false")) multiplexer_2 (
    .in0(ram_1_data), .in1(signextend_1_signextvalue), .out(multiplexer_2_out), .sel(undriven_5));
  ALU alu_1 (.AC(AC_q), .Y(multiplexer_2_out), .ALUOp(undriven_6), .Output(alu_1_output));  // open: Overflow

  // Notes on the sheet:
  //   Control Wires
  //   Data Memory
  //   MemWr
  //   Clock
  //   Sign Extend
  //   WriteAC
  //   ClrAC
  //   Mem Data
  //   Immediate
  //   Select ALU Input
  //   ALUSrc
  //   AC to ALU
  //   ALUOpt
  //   ALU to AC
  //   ALU
endmodule

module CPU___Execution_Control (
);

  wire and_1_out, clock_1_out, comparator_1_eq, control_unit_1_p2, control_unit_1_p3, control_unit_1_p4,
       control_unit_1_p5, control_unit_1_p6, control_unit_1_p7;
  wire [7:0] adder_1_out, multiplexer_1_out, PC_q, ram_1_data;
  wire [15:0] undriven;
  wire [15:8] ram_1_data_2;

  Clock clock_1 (.out(clock_1_out));
  Adder adder_1 (.a(PC_q), .b(8'h1), .out(adder_1_out));  // open: cin, cout
  and and_1 (and_1_out, comparator_1_eq, control_unit_1_p7);
  Multiplexer #(.width(8), .enable("false")) multiplexer_1 (
    .in0(adder_1_out), .in1(ram_1_data), .out(multiplexer_1_out), .sel(and_1_out));
  Register PC (.D(multiplexer_1_out), .en(1'b1), .Q(PC_q), .clk(clock_1_out));  // open: clr
  RAM #(.dataWidth(16)) ram_1 (
    .addr(PC_q), .data({ram_1_data_2, ram_1_data}), .clk(clock_1_out));  // open: sel, ld, clr
  // Control_Unit control_unit_1: pin names not known; wires that end beside it: ram_1_data_2, control_unit_1_p2, control_unit_1_p3, control_unit_1_p4, control_unit_1_p5, control_unit_1_p6, control_unit_1_p7
  Comparator #(.width(16)) comparator_1 (.a(undriven), .b({16{1'b0}}), .eq(comparator_1_eq));  // open: gt, lt

  // Notes on the sheet:
  //   Reset PC
  //   Increment PC
  //   Branch Address
  //   Next Instr
  //   Select Branch if Branc = true and ALU is zero
  //   Text (Program) Memory
  //   Immediate Value to DM
  //   Immediate Value to ALU
  //   Control Unit
  //   Beqz
  //   Value From ALU
  //   Comparator
endmodule

module ALU1 (
  input  [15:0] AC,
  input  [15:0] Y,
  input  [3:0] ALUOp,
  output [15:0] Output
);

  wire [15:0] adder_1_out, and_1_out, divider_1_out, divider_1_rem, multiplier_1_out, shifter_1_out,
       subtractor_1_out;

  Adder #(.width(16)) adder_1 (.a(AC), .b(Y), .out(adder_1_out));  // open: cin, cout
  Subtractor #(.width(16)) subtractor_1 (.a(AC), .b(Y), .out(subtractor_1_out));  // open: bin, bout
  Multiplier #(.width(16)) multiplier_1 (.a(AC), .b(Y), .out(multiplier_1_out));  // open: cin, cout
  Divider #(.width(16)) divider_1 (.a(AC), .b(Y), .out(divider_1_out), .rem(divider_1_rem));  // open: upper
  assign and_1_out = AC & Y;  // AND_Gate and_1, 16 bits wide
  Shifter #(.width(16)) shifter_1 (.in(AC), .\dist (Y[3:0]), .out(shifter_1_out));
  Multiplexer #(.select(4), .width(16), .enable("false")) multiplexer_1 (
    .in0(adder_1_out), .in1(subtractor_1_out), .in2(multiplier_1_out), .in3(divider_1_out),
    .in4(divider_1_rem), .in5(and_1_out), .in6(shifter_1_out), .out(Output), .sel(ALUOp));  // open: in7, in8, in9, in10, in11, in12, in13, in14, in15

  // Notes on the sheet:
  //   0000 = add
  //   0001 = sub
  //   0010 = mul
  //   0011 = div
  //   0100 = rem
  //   0101 = and
  //   0110 = shift
endmodule

module _2_3_CPU_main (
);

  wire and_1_out, button_1_out, clock_1_out, comparator_1_eq, Control_alusrc, Control_branch,
       Control_memread, Control_memwrite, Control_mentoreg, Control_regdst, Control_regwrite;
  wire [1:0] Control_aluop;
  wire [3:0] ALU_control_alu_control;
  wire [4:0] multiplexer_2_out;
  wire [15:0] adder_1_out, adder_2_out, multiplexer_1_out, PC_q, ram_1_data;
  wire [31:0] ALU_output, multiplexer_3_out, multiplexer_4_out, ram_2_data, Registers_read_data_1,
       Registers_read_data_2, Sign_Extend_signextvalue;
  wire [31:16] ram_1_data_2;

  Clock clock_1 (.out(clock_1_out));
  Button button_1 (.out(button_1_out));
  Adder #(.width(16)) adder_1 (.a(PC_q), .b(16'h1), .out(adder_1_out));  // open: cin, cout
  Multiplexer #(.width(16), .enable("false")) multiplexer_1 (
    .in0(adder_1_out), .in1(adder_2_out), .out(multiplexer_1_out), .sel(and_1_out));
  Adder #(.width(16)) adder_2 (.a(adder_1_out), .b(ram_1_data), .out(adder_2_out));  // open: cin, cout
  and and_1 (and_1_out, comparator_1_eq, Control_branch);
  Register #(.width(16)) PC (.D(multiplexer_1_out), .en(1'b1), .Q(PC_q), .clk(clock_1_out), .clr(button_1_out));
  RAM #(.addrWidth(16), .dataWidth(32)) ram_1 (
    .addr(PC_q), .data({ram_1_data_2, ram_1_data}), .clk(clock_1_out));  // open: sel, ld, clr
  Multiplexer #(.width(5), .enable("false")) multiplexer_2 (
    .in0(ram_1_data_2[20:16]), .in1(ram_1_data[15:11]), .out(multiplexer_2_out), .sel(Control_regdst));
  Shifter #(.width(16)) shifter_1 (.in(ram_1_data), .\dist (4'b0001));  // open: out
  Registers Registers (
    .Register_1_address(ram_1_data_2[25:21]), .Register_2_address(ram_1_data_2[20:16]),
    .Write_Register_address(multiplexer_2_out), .Write_data(multiplexer_4_out),
    .Read_data_1(Registers_read_data_1), .Read_data_2(Registers_read_data_2), .RegWrite(Control_regwrite),
    .Clock(clock_1_out));
  Control_Unit_2 Control (
    .Opcode(ram_1_data_2[31:26]), .RegDst(Control_regdst), .Branch(Control_branch),
    .MemRead(Control_memread), .MenToReg(Control_mentoreg), .ALUOp(Control_aluop),
    .MemWrite(Control_memwrite), .ALUSrc(Control_alusrc), .RegWrite(Control_regwrite));
  _16_32_SignExtend Sign_Extend (.Immediate(ram_1_data), .SignExtValue(Sign_Extend_signextvalue));
  Multiplexer #(.width(32), .enable("false")) multiplexer_3 (
    .in0(Registers_read_data_2), .in1(Sign_Extend_signextvalue), .out(multiplexer_3_out), .sel(Control_alusrc));
  ALU_control ALU_control (
    .Funct(ram_1_data[5:0]), .Opcode(ram_1_data_2[31:26]), .ALU_Op(Control_aluop),
    .ALU_control(ALU_control_alu_control));
  ALU2 ALU (
    .in_1(Registers_read_data_1), .in_2(multiplexer_3_out), .ALUOp(ALU_control_alu_control),
    .Output(ALU_output));
  Comparator #(.width(32)) comparator_1 (.a(ALU_output), .b({32{1'b0}}), .eq(comparator_1_eq));  // open: gt, lt
  RAM #(.dataWidth(32), .bus("separate")) ram_2 (
    .addr(ALU_output[7:0]), .din(Registers_read_data_2), .data(ram_2_data), .str(Control_memwrite),
    .sel(1'b1), .clk(clock_1_out), .ld(Control_memread));  // open: clr
  Multiplexer #(.width(32), .enable("false")) multiplexer_4 (
    .in0(ALU_output), .in1(ram_2_data), .out(multiplexer_4_out), .sel(Control_mentoreg));

  // Notes on the sheet:
  //   Increment PC
  //   Branch Address
  //   Next Instr
  //   Select Branch if Branc = true and ALU is zero
  //   Text (Program) Memory
  //   Shift left
  //   RegDst
  //   ALU Src
  //   MemToReg
endmodule

module Registers (
  input  [4:0] Register_1_address,
  input  [4:0] Register_2_address,
  input  [4:0] Write_Register_address,
  input  [31:0] Write_data,
  input  RegWrite,
  input  Clock,
  output [31:0] Read_data_1,
  output [31:0] Read_data_2
);

  wire decoder_1_out0, decoder_1_out1, decoder_1_out2, decoder_1_out3, decoder_1_out4, decoder_1_out5,
       decoder_1_out6, decoder_1_out7, decoder_1_out8, decoder_1_out9, decoder_1_out10, decoder_1_out11;
  wire [31:0] a0_q, a1_q, a2_q, a3_q, at_q, t0_q, t1_q, t2_q, t3_q, v0_q, v1_q, zero_q;

  Decoder #(.select(5)) decoder_1 (
    .out0(decoder_1_out0), .out1(decoder_1_out1), .out2(decoder_1_out2), .out3(decoder_1_out3),
    .out4(decoder_1_out4), .out5(decoder_1_out5), .out6(decoder_1_out6), .out7(decoder_1_out7),
    .out8(decoder_1_out8), .out9(decoder_1_out9), .out10(decoder_1_out10), .out11(decoder_1_out11),
    .sel(Write_Register_address), .en(RegWrite));  // open: out12, out13, out14, out15, out16, out17, out18, out19, out20, out21, out22, out23, out24, out25, out26, out27, out28, out29, out30, out31
  Register #(.width(32)) zero (.D(Write_data), .Q(zero_q));  // open: en, clk, clr
  Register #(.width(32)) at (.D(Write_data), .en(decoder_1_out1), .Q(at_q), .clk(Clock));  // open: clr
  Register #(.width(32)) v0 (.D(Write_data), .en(decoder_1_out2), .Q(v0_q), .clk(Clock));  // open: clr
  Register #(.width(32)) v1 (.D(Write_data), .en(decoder_1_out3), .Q(v1_q), .clk(Clock));  // open: clr
  Register #(.width(32)) a0 (.D(Write_data), .en(decoder_1_out4), .Q(a0_q), .clk(Clock));  // open: clr
  Register #(.width(32)) a1 (.D(Write_data), .en(decoder_1_out5), .Q(a1_q), .clk(Clock));  // open: clr
  Register #(.width(32)) a2 (.D(Write_data), .en(decoder_1_out6), .Q(a2_q), .clk(Clock));  // open: clr
  Register #(.width(32)) a3 (.D(Write_data), .en(decoder_1_out7), .Q(a3_q), .clk(Clock));  // open: clr
  Register #(.width(32)) t0 (.D(Write_data), .en(decoder_1_out8), .Q(t0_q), .clk(Clock));  // open: clr
  Register #(.width(32)) t1 (.D(Write_data), .en(decoder_1_out9), .Q(t1_q), .clk(Clock));  // open: clr
  Register #(.width(32)) t2 (.D(Write_data), .en(decoder_1_out10), .Q(t2_q), .clk(Clock));  // open: clr
  Register #(.width(32)) t3 (.D(Write_data), .en(decoder_1_out11), .Q(t3_q), .clk(Clock));  // open: clr
  Multiplexer #(.select(5), .width(32)) multiplexer_1 (
    .in0(zero_q), .in1(at_q), .in2(v0_q), .in3(v1_q), .in4(a0_q), .in5(a1_q), .in6(a2_q), .in7(a3_q),
    .in8(t0_q), .in9(t1_q), .in10(t2_q), .in11(t3_q), .out(Read_data_1), .sel(Register_1_address));  // open: in12, in13, in14, in15, in16, in17, in18, in19, in20, in21, in22, in23, in24, in25, in26, in27, in28, in29, in30, in31, en
  Multiplexer #(.select(5), .width(32)) multiplexer_2 (
    .in0(zero_q), .in1(at_q), .in2(v0_q), .in3(v1_q), .in4(a0_q), .in5(a1_q), .in6(a2_q), .in7(a3_q),
    .in8(t0_q), .in9(t1_q), .in10(t2_q), .in11(t3_q), .out(Read_data_2), .sel(Register_2_address));  // open: in12, in13, in14, in15, in16, in17, in18, in19, in20, in21, in22, in23, in24, in25, in26, in27, in28, in29, in30, in31, en
endmodule

module _16_32_SignExtend (
  input  [15:0] Immediate,
  output [31:0] SignExtValue
);


  assign SignExtValue = {{17{Immediate[15]}}, Immediate[14:0]};
endmodule

module ALU2 (
  input  [31:0] in_1,
  input  [31:0] in_2,
  input  [3:0] ALUOp,
  output [31:0] Output
);

  wire [31:0] adder_1_out, and_1_out, divider_1_out, divider_1_rem, multiplier_1_out, subtractor_1_out;

  Adder #(.width(32)) adder_1 (.a(in_1), .b(in_2), .out(adder_1_out));  // open: cin, cout
  Subtractor #(.width(32)) subtractor_1 (.a(in_1), .b(in_2), .out(subtractor_1_out));  // open: bin, bout
  Multiplier #(.width(32)) multiplier_1 (.a(in_1), .b(in_2), .out(multiplier_1_out));  // open: cin, cout
  Divider #(.width(32)) divider_1 (.a(in_1), .b(in_2), .out(divider_1_out), .rem(divider_1_rem));  // open: upper
  assign and_1_out = in_1 & in_2;  // AND_Gate and_1, 32 bits wide
  Multiplexer #(.select(4), .width(32), .enable("false")) multiplexer_1 (
    .in0(adder_1_out), .in1(subtractor_1_out), .in2(multiplier_1_out), .in3(divider_1_out),
    .in4(divider_1_rem), .in5(and_1_out), .out(Output), .sel(ALUOp));  // open: in6, in7, in8, in9, in10, in11, in12, in13, in14, in15

  // Notes on the sheet:
  //   0000 = add
  //   0001 = sub
  //   0010 = mul
  //   0011 = div
  //   0100 = rem
  //   0101 = and
endmodule

module ALU_control (
  input  [5:0] Funct,
  input  [5:0] Opcode,
  input  [1:0] ALU_Op,
  output [3:0] ALU_control
);

  wire [3:0] rom_1_data, rom_2_data;

  ROM #(.addrWidth(6), .dataWidth(4)) rom_1 (.addr(Funct), .data(rom_1_data));  // open: sel
  ROM #(.addrWidth(6), .dataWidth(4)) rom_2 (.addr(Opcode), .data(rom_2_data));  // open: sel
  Multiplexer #(.select(2), .width(4)) multiplexer_1 (
    .in0(4'b0010), .in1(4'b0110), .in2(rom_1_data), .in3(rom_2_data), .out(ALU_control), .sel(ALU_Op));  // open: en

  // Notes on the sheet:
  //   using opcode for I intruction
  //   contents of rom_2 (hex, n*v repeats v):
  //   1
endmodule

module Control_Unit_2 (
  input  [5:0] Opcode,
  output RegDst,
  output Branch,
  output MemRead,
  output MenToReg,
  output [1:0] ALUOp,
  output MemWrite,
  output ALUSrc,
  output RegWrite
);

  ROM #(.addrWidth(6), .dataWidth(9)) rom_1 (
    .addr(Opcode), .data({RegWrite, ALUSrc, MemWrite, ALUOp, MenToReg, MemRead, Branch, RegDst}));  // open: sel

  // Notes on the sheet:
  //   contents of rom_1 (hex, n*v repeats v):
  //   1
endmodule
